# Fritzing sketch pspi1 (saved by Fritzing 0.9.3b)
circuit board: 2.54942cm x 2.01318cm
breadboards: 1

parts:
  Ventola = DC Motor
  Diodo = Rectifier Diode [package="300 mil [THT]"]
  Transistor = NPN-Transistor [package="TO92 [THT]"]
  Componente1 = Arduino Uno (Rev3)
  Caricatore = 4 x AAA Battery Mount

nets:
  N1: Ventola.pin_1, Diodo.cathode, Caricatore.+
  N2: Ventola.pin_2, Diodo.anode, Transistor.C
  N3: Transistor.E, Componente1.GND, Caricatore.-
  N4: Transistor.B, Componente1.D4
