# Fritzing sketch pspi2.1 (saved by Fritzing 0.9.3b)
circuit board: 4.71744cm x 4.28062cm
breadboards: 1

parts:
  Ventola = DC Motor
  Transistor = NPN-Transistor [package="TO92 [THT]"]
  Componente1 = Arduino Uno (Rev3)
  Caricatore_a_5V = 4 x AAA Battery Mount
  R1 = Resistor [tolerance=±5% resistance=10k package=THT]
  Sensore_temperatura = DS18B20 1-Wire Temperature Sensor [part_number=DS18B20]
  J1 = Screw terminal - 2 pins [package=THT]
  J2 = Screw terminal - 2 pins [package=THT]
  J3 = Screw terminal - 2 pins [package=THT]
  J4 = Screw terminal - 2 pins [package=THT]
  J5 = Screw terminal - 2 pins [package=THT]
  J6 = Screw terminal - 2 pins [package=THT]

nets:
  N1: Ventola.pin_1, Transistor.E, J6.pin1
  GND: Ventola.pin_2, Componente1.GND, Caricatore_a_5V.-, Sensore_temperatura.GND, J1.pin1, J2.pin1, J5.pin2, J6.pin2
  N2: Transistor.B, Componente1.D4, J2.pin2
  N3: Transistor.C, Caricatore_a_5V.+, J1.pin2
  N4: Componente1.D2, R1.Pin_0, Sensore_temperatura.DQ, J3.pin2, J4.pin1
  5V: Componente1.5V, R1.Pin_1, Sensore_temperatura.VDD, J3.pin1, J4.pin2
