# Fritzing sketch pspi2.2 (saved by Fritzing 0.9.3b)
circuit board: 6.26026cm x 4.34647cm
breadboards: 1

parts:
  Ventola = DC Motor
  Transistor = NPN-Transistor [package="TO92 [THT]"]
  Componente1 = Arduino Uno (Rev3)
  Caricatore_a_5V = 4 x AAA Battery Mount
  R1 = Resistor [tolerance=±5% resistance=10k package=THT]
  Sensore_temperatura = DS18B20 1-Wire Temperature Sensor [part_number=DS18B20]
  J1 = Screw terminal - 2 pins [package=THT]
  J2 = Screw terminal - 2 pins [package=THT]
  J3 = Screw terminal - 2 pins [package=THT]
  J4 = Screw terminal - 2 pins [package=THT]
  J5 = Screw terminal - 2 pins [package=THT]
  J6 = Screw terminal - 2 pins [package=THT]
  Relay_per_il_calore = OMRON PCB Power Relay – G5LE [part_number="G5LE-1\n" package=THT]
  J7 = Screw terminal - 2 pins [package=THT]
  J8 = Screw terminal - 2 pins [package=THT]
  J10 = Screw terminal - 2 pins [package=THT]
  J11 = Screw terminal - 2 pins [package=THT]
  LED1 = LED - 5mm [color="Red (633nm)" package="5 mm [THT]"]
  R2 = Resistor [tolerance=±5% resistance=220 package=THT]
  Fotoresistore = PHOTOCELL [package=photocell-kit]
  R3 = Resistor [tolerance=±5% resistance=100k package=THT]
  J12 = Screw terminal - 2 pins [package=THT]

nets (from the pcb view):
  N1: Ventola.pin_1, Caricatore_a_5V.+, J1.pin2, J6.pin1
  N2: Ventola.pin_2, Transistor.C, J6.pin2
  GND: Transistor.E, Componente1.GND, Caricatore_a_5V.-, Sensore_temperatura.GND, J1.pin1, J2.pin1, J5.pin2, Relay_per_il_calore.COIL2, J7.pin1, J10.pin2, J11.pin1, LED1.cathode, Fotoresistore.P$2
  N3: Transistor.B, Componente1.D4, J2.pin2
  N4: Componente1.A0, J8.pin1, J10.pin1, Fotoresistore.P$1, R3.Pin_0
  N5: Componente1.D2, R1.Pin_0, Sensore_temperatura.DQ, J3.pin2, J4.pin1
  N6: Componente1.D3_PWM, J5.pin1, Relay_per_il_calore.C, J7.pin2
  N7: Componente1.D5_PWM, R2.Pin_1, J12.pin2
  5V: Componente1.5V, R1.Pin_1, Sensore_temperatura.VDD, J3.pin1, J4.pin2, Relay_per_il_calore.COIL1, J8.pin2, R3.Pin_1
  N8: J11.pin2, LED1.anode, R2.Pin_0
