# Fritzing sketch pspi2 (saved by Fritzing 0.9.3b)
circuit board: 4.49166cm x 2.57319cm
breadboards: 1

parts:
  Ventola = DC Motor
  Diodo = Rectifier Diode [part_number=1N4001 package="300 mil [THT]"]
  Transistor = NPN-Transistor [package="TO92 [THT]"]
  Componente1 = Arduino Uno (Rev3)
  Caricatore = 4 x AAA Battery Mount
  R1 = Resistor [tolerance=±5% resistance=10k package=THT]
  DS2 = DS18B20 1-Wire Temperature Sensor [part_number=DS18B20]
  J1 = Screw terminal - 2 pins [package=THT]
  J2 = Screw terminal - 2 pins [package=THT]
  J3 = Screw terminal - 2 pins [package=THT]
  J4 = Screw terminal - 2 pins [package=THT]
  J5 = Screw terminal - 2 pins [package=THT]

nets:
  N1: Ventola.pin_1, Diodo.cathode, Caricatore.+, J1.pin2
  N2: Ventola.pin_2, Diodo.anode, Transistor.C
  GND: Transistor.E, Componente1.GND, Caricatore.-, DS2.GND, J1.pin1, J5.pin2
  N3: Transistor.B, Componente1.D4, J2.pin2
  N4: Componente1.D2, R1.Pin_0, DS2.DQ, J2.pin1, J4.pin1
  5V: Componente1.5V, R1.Pin_1, DS2.VDD, J3.pin2, J4.pin2
