# Fritzing sketch pspi3.0 (saved by Fritzing 0.9.3b)
circuit board: 9.47017cm x 2.63395cm
breadboards: 1

parts:
  J2 = female pin header, 2 pins [form="♀ (female)"]
  J3 = female pin header, 2 pins [form="♀ (female)"]
  J4 = female pin header, 2 pins [form="♀ (female)"]
  J5 = female pin header, 2 pins [form="♀ (female)"]
  J6 = female pin header, 2 pins [form="♀ (female)"]
  J7 = female pin header, 2 pins [form="♀ (female)"]
  J8 = female pin header, 2 pins [form="♀ (female)"]
  J9 = female pin header, 2 pins [form="♀ (female)"]
  J10 = female pin header, 2 pins [form="♀ (female)"]  # not connected
  J11 = female pin header, 2 pins [form="♀ (female)"]  # not connected
  J12 = female pin header, 2 pins [form="♀ (female)"]  # not connected
  VCC1 = 4 x AAA Battery Mount

nets:
  N1: J2.pin1, J3.pin1, J4.pin1, J6.pin2, J7.pin1, J8.pin1, J9.pin2, VCC1.-
  N2: J2.pin2, J3.pin2, VCC1.+
  N3: J4.pin2, J5.pin1, J8.pin2, J9.pin1
